// Logisim project summator.circ as structural Verilog: 1 circuit, main circuit main
module main (
  input  C_in,
  input  A0,
  input  B0,
  input  [7:0] in_4,
  input  [7:0] in_5,
  input  C_in_2,
  input  Cout,
  output S0,
  output Cout_2,
  output [7:0] out_10
);

  wire and_1_out, and_2_out, and_3_out, and_4_out, and_5_out, and_6_out, and_7_out, and_8_out, and_9_out,
       and_10_out, and_11_out, and_12_out, and_13_out, and_14_out, and_15_out, and_16_out, and_17_out,
       and_18_out, or_2_out, or_3_out, or_4_out, or_5_out, or_6_out, or_7_out, or_8_out, xor_1_out,
       xor_3_out, xor_5_out, xor_7_out, xor_9_out, xor_11_out, xor_13_out, xor_15_out, xor_17_out;

  // Probe on in_4
  // Probe on {in_5[7:6], in_4[5], in_5[4:0]}
  // Probe on out_10
  xor xor_1 (xor_1_out, A0, B0);
  and and_1 (and_1_out, B0, A0);
  xor xor_2 (S0, C_in, xor_1_out);
  and and_2 (and_2_out, xor_1_out, C_in);
  xor xor_3 (xor_3_out, in_4[0], in_5[0]);
  and and_3 (and_3_out, in_5[0], in_4[0]);
  or or_1 (Cout_2, and_2_out, and_1_out);
  and and_4 (and_4_out, xor_3_out, C_in_2);
  xor xor_4 (out_10[0], C_in_2, xor_3_out);
  or or_2 (or_2_out, and_4_out, and_3_out);
  xor xor_5 (xor_5_out, in_4[1], in_5[1]);
  and and_5 (and_5_out, in_5[1], in_4[1]);
  xor xor_6 (out_10[1], or_2_out, xor_5_out);
  and and_6 (and_6_out, xor_5_out, or_2_out);
  or or_3 (or_3_out, and_6_out, and_5_out);
  xor xor_7 (xor_7_out, in_4[2], in_5[2]);
  and and_7 (and_7_out, in_5[2], in_4[2]);
  xor xor_8 (out_10[2], or_3_out, xor_7_out);
  and and_8 (and_8_out, xor_7_out, or_3_out);
  or or_4 (or_4_out, and_8_out, and_7_out);
  xor xor_9 (xor_9_out, in_4[3], in_5[3]);
  and and_9 (and_9_out, in_5[3], in_4[3]);
  xor xor_10 (out_10[3], or_4_out, xor_9_out);
  and and_10 (and_10_out, xor_9_out, or_4_out);
  or or_5 (or_5_out, and_10_out, and_9_out);
  xor xor_11 (xor_11_out, in_4[4], in_5[4]);
  and and_11 (and_11_out, in_5[4], in_4[4]);
  xor xor_12 (out_10[4], or_5_out, xor_11_out);
  and and_12 (and_12_out, xor_11_out, or_5_out);
  or or_6 (or_6_out, and_12_out, and_11_out);
  xor xor_13 (xor_13_out, in_4[5], in_4[5]);
  and and_13 (and_13_out, in_4[5], in_4[5]);
  xor xor_14 (out_10[5], or_6_out, xor_13_out);
  and and_14 (and_14_out, xor_13_out, or_6_out);
  or or_7 (or_7_out, and_14_out, and_13_out);
  xor xor_15 (xor_15_out, in_4[6], in_5[6]);
  and and_15 (and_15_out, in_5[6], in_4[6]);
  and and_16 (and_16_out, xor_15_out, or_7_out);
  xor xor_16 (out_10[6], or_7_out, xor_15_out);
  or or_8 (or_8_out, and_16_out, and_15_out);
  xor xor_17 (xor_17_out, in_4[7], in_5[7]);
  and and_17 (and_17_out, in_5[7], in_4[7]);
  and and_18 (and_18_out, xor_17_out, or_8_out);
  xor xor_18 (out_10[7], or_8_out, xor_17_out);
  or or_9 (Cout, and_18_out, and_17_out);

  assign in_5[5] = in_4[5];
endmodule
