// Logisim project digital_app.circ as structural Verilog: 1 circuit, main circuit main
module main (
  output [2:0] out_1
);

  wire and_1_out, clock_1_out, not_1_out, not_2_out;

  Clock clock_1 (.out(clock_1_out));
  T_Flip_Flop Q0 (.clk(clock_1_out), .T(1'b1), .Q(out_1[0]));  // open: Qn, preset, reset, en
  T_Flip_Flop Q1 (.clk(clock_1_out), .T(not_1_out), .Q(out_1[1]));  // open: Qn, preset, reset, en
  not not_1 (not_1_out, out_1[0]);
  // Probe on out_1
  and and_1 (and_1_out, not_2_out, not_1_out);
  not not_2 (not_2_out, out_1[1]);
  T_Flip_Flop Q2 (.clk(clock_1_out), .T(and_1_out), .Q(out_1[2]));  // open: Qn, preset, reset, en
endmodule
